# Fritzing sketch mahmoud project (saved by Fritzing 0.9.5d)
breadboards: 1

parts:
  M1 = ESP32-S3-DevKitC-1-N8R8-v1 [part_number=ESP32-S3-DevKitC-1-N8R8-v1]
  J1 = Basic Servo
  J2 = Basic Servo
  Part1 = InvenSense MPU6050
  Part2 = AHT20 BMP280 pressure and humidity breakout
  TSYS1 = TSYS01 [package="SIP (Single Inline) [THT]"]
  Part3 = HX711 Weighing Sensor Module
  S1 = H-Bridge with L298N
  TEC1 = TEC1-12706 Thermo Electric Cooler [package=THT]
  Load_Cell1 = Load Cell - Red/white/black/green
  VALVE1 = Plastic Solenoid Valve
  WATER_PUMP1 = water pump/motor
  Q2 = MOSFET-NCHANNEL [package=to220v]
  F1 = Small Fan, based on Fan - Ventilador [package=THT]
  D2 = Rectifier Diode [part_number=1N4001 package="300 mil [THT]"]
  D3 = Rectifier Diode [part_number=1N4001 package="300 mil [THT]"]
  D4 = Rectifier Diode [part_number=1N4001 package="300 mil [THT]"]
  Q3 = MOSFET-NCHANNEL [package=to220v]
  Q4 = MOSFET-NCHANNEL [package=to220v]
  Part4 = Lithium Ion Battery Pack 3.7V 6600mAh [part_number=353]
  Part5 = Lithium Ion Polymer Battery 3.7v 100mAh [part_number=1570]

nets:
  VCC: M1.pin_1, M1.pin_2, J1.vcc, J2.vcc, Part1.VCC, Part2.VDD, TSYS1.VDD, Part3.VCC, Part5.positive
  N1: M1.pin_4, Part3.DO/RX
  N2: M1.pin_5, Part3.CK/TX
  N3: M1.pin_15, Q4.G
  N4: M1.pin_18, Q3.G
  GND: M1.pin_22, M1.pin_23, M1.pin_24, M1.pin_44, J1.gnd, J2.gnd, Part1.GND, Part2.GND, TSYS1.GND, Part3.GND, Q2.S, Q3.S, Q4.S, Part4.negative, Part5.negative
  N5: M1.pin_29, J2.pulse
  N6: M1.pin_30, J1.pulse
  N7: M1.pin_32, S1.IN2
  N8: M1.pin_33, S1.IN1
  N9: M1.pin_34, S1.ENA
  N10: M1.pin_35, Q2.G
  N11: M1.pin_37, Part1.SCL, Part2.SCL, TSYS1.SCL
  N12: M1.pin_39, Part1.SDA, Part2.SDA, TSYS1.SDA
  N13: Part3.E+, Load_Cell1.wire1
  N14: Part3.E-, Load_Cell1.wire3
  N15: Part3.A+, Load_Cell1.wire4
  N16: Part3.A-, Load_Cell1.wire2
  N17: S1.M1-01, TEC1.+
  N18: S1.M1-02, TEC1.-
  N19: VALVE1.no_name_yet#1, D3.anode, Q4.D
  N20: VALVE1.no_name_yet#2, WATER_PUMP1.pin_2, F1.5V, D2.cathode, D3.cathode, D4.cathode, Part4.positive
  N21: WATER_PUMP1.pin_1, D4.anode, Q3.D
  N22: Q2.D, F1.GND, D2.anode

custom parts:
  ESP32-S3-DevKitC-1-N8R8-v1: ESP32-S3-DevKitC-1-N8R8-v1 This module is 44pins long (2x22) and 11 pins width.
  AHT20 BMP280 pressure and humidity breakout: Cheap breakout board for the BMP280, barometric pressure sensor, and AHT20, humidity sensor
  TSYS01: Temperature sensor I2C 0.1 degrees accurate
  H-Bridge with L298N: h-bridge
  Load Cell - Red/white/black/green: A rectangle load cell/weighting pressure Sensor with four wires - Red, white, black, green. Normally corresponding with E+, E-, A+, A- respectively.
  water pump/motor: WATER PUMP BY ARDUBLOCKTR
  Small Fan, based on Fan - Ventilador: Small 2-pin fan, commonly used with single-board computers, 3d-printers, etc. This work is based on a much larger fan, as commonly found in desktop computers
  Lithium Ion Battery Pack 3.7V 6600mAh: This lithium ion pack is made of 3 balanced 2200mAh cells for a total of 6600mA capacity! The cells are connected in parallel and spot-welded to a protection circuit that provides over-voltage, under-voltage and over-current protection. Each cell can provide 0.5C of current (1.1 A per) so all together the peak current you can draw is over 3.3 Amps. Note that these batteries are not designed to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
  Lithium Ion Polymer Battery 3.7v 100mAh: Lithium ion polymer (also known as 'lipo' or 'lipoly') batteries are thin, light and powerful. The output ranges from 4.2V when completely charged to 3.7V. This battery has a capacity of ~100mAh for a total of about 0.4 Wh. The batteries come pre-attached with a genuine 2-pin JST-PH connector as shown and include the necessary protection circuitry.
